# Fritzing sketch Schematic (Turn Signal and Counter) (saved by Fritzing 0.9.3b)
breadboards: 1

parts:
  Part1 = Arduino Mega 2560 (Rev3)
  LED1 = smd LED [color="Red (633nm)" package="0805 [SMD]"]
  LED2 = smd LED [color="Yellow (595nm)" package="0805 [SMD]"]
  LED3 = smd LED [color="Red (633nm)" package="0805 [SMD]"]
  LED4 = smd LED [color="Yellow (595nm)" package="0805 [SMD]"]
  LED5 = smd LED [color="Red (633nm)" package="0805 [SMD]"]
  LED7 = LED - 5mm [color="Red (633nm)" package="5 mm [THT]"]
  LED8 = LED - 5mm [color="Yellow (595nm)" package="5 mm [THT]"]
  LED9 = smd LED [color="Red (633nm)" package="0805 [SMD]"]
  LED10 = smd LED [color="Yellow (595nm)" package="0805 [SMD]"]
  7_Segment1 = 7-Segment LED Display [package=THT]
  R1 = Rotary Potentiometer (Small) [maximum_resistance=10kΩ package=THT]
  LED11 = LED - 5mm [color="Red (633nm)" package="5 mm [THT]"]

nets:
  N1: Part1.A0, R1.leg2
  N2: Part1.D21/SCL, 7_Segment1.cathodeG
  N3: Part1.D20/SDA, 7_Segment1.cathodeF
  N4: Part1.D19/RX1, 7_Segment1.cathodeE
  N5: Part1.D18/TX1, 7_Segment1.cathodeD
  N6: Part1.D17_PWM/RX2, 7_Segment1.cathodeC
  N7: Part1.D16_PWM/TX2, 7_Segment1.cathodeB
  N8: Part1.D15/RX3, 7_Segment1.cathodeA
  N9: Part1.GND, LED4.cathode, LED5.cathode, LED7.cathode, LED8.cathode, LED9.cathode, LED10.cathode, 7_Segment1.commAnode#2, R1.leg1, LED11.cathode
  N10: Part1.5V, R1.wiper
  N11: Part1.D2_PWM, LED3.anode, LED5.anode, LED7.anode
  N12: Part1.D3_PWM, LED9.anode, LED11.anode
  N13: Part1.D4_PWM, LED4.anode
  N14: Part1.D5_PWM, LED8.anode
  N15: Part1.D6_PWM, LED10.anode
  N16: Part1.D7_PWM, LED2.anode
  N17: LED1.cathode, LED2.cathode, LED3.cathode
