# Fritzing sketch Schematic (LM35 Sensor) (saved by Fritzing 0.9.3b)
breadboards: 1

parts:
  Part1 = Arduino Mega ADK (Rev3)
  T1 = LM35 Temperature Sensor [package="TO92 [THT]"]
  LED1 = LED - 3mm [color="Red (633nm)" package="3 mm [THT]"]
  LED2 = LED - 3mm [color="Red (633nm)" package="3 mm [THT]"]
  LED3 = LED - 3mm [color="Red (633nm)" package="3 mm [THT]"]

nets:
  N1: Part1.A0, T1.Vout
  N2: Part1.5V, T1.+Vs
  GND: Part1.GND, T1.GND, LED1.cathode, LED2.cathode, LED3.cathode
  N3: Part1.D5_PWM, LED2.anode
  N4: Part1.D7_PWM, LED1.anode

notes:
  Semáforo de temperatura con sensor LM35
