# Fritzing sketch Schematic (LDR Sensor) (saved by Fritzing 0.9.3b)
breadboards: 1

parts:
  Part1 = Arduino Mega ADK (Rev3)
  LED1 = LED - 3mm [color="Red (633nm)" package="3 mm [THT]"]
  LED2 = LED - 3mm [color="Red (633nm)" package="3 mm [THT]"]
  LED3 = LED - 3mm [color="Red (633nm)" package="3 mm [THT]"]
  R1 = Photocell (LDR) [package=THT]
  R2 = Resistor [tolerance=±5% resistance=10k package=THT]

nets:
  N1: Part1.A0, R2.Pin_1
  N2: Part1.5V, R1.pin_0
  N3: Part1.GND, R1.pin_1, R2.Pin_0
  N4: Part1.D5_PWM, LED2.anode
  N5: Part1.D7_PWM, LED1.anode
  N6: LED1.cathode, LED2.cathode, LED3.cathode

notes:
  Semáforo de luminosidad con fotorresistencia
  Pull-down resistor 10kΩ
