# Fritzing sketch Schematic (CNY70 Sensor) (saved by Fritzing 0.9.3b)
breadboards: 1

parts:
  Part1 = Arduino Mega ADK (Rev3)
  LED1 = LED - 3mm [color="Red (633nm)" package="3 mm [THT]"]
  LED2 = LED - 3mm [color="Red (633nm)" package="3 mm [THT]"]
  U1 = Sharp PC817 [package=THT]
  R3 = Resistor [tolerance=±5% resistance=220 package=THT]
  R4 = Resistor [tolerance=±5% resistance=10k package=THT]
  R5 = Resistor [tolerance=±5% resistance=220 package=THT]
  R6 = Resistor [tolerance=±5% resistance=220 package=THT]

nets:
  N1: Part1.5V, U1.Pin_2, U1.Pin_4
  N2: Part1.GND, LED1.cathode, LED2.cathode, R3.Pin_0
  N3: Part1.D1/TX0, U1.Pin_3, R4.Pin_0
  N4: Part1.D5_PWM, R6.Pin_0
  N5: Part1.D7_PWM, R5.Pin_0
  N6: LED1.anode, R5.Pin_1
  N7: LED2.anode, R6.Pin_1
  N8: U1.Pin_1, R3.Pin_1

notes:
  Detector de colores blanco/negro con sensor óptico CNY70
  CNY70
  Lado izq. Emisor
  Lado der. Colector
  R2 10kΩ
  R1 220Ω
