# Fritzing sketch Schematic (Push Button and Roller Lever) (saved by Fritzing 0.9.3b)
breadboards: 1

parts:
  Part1 = Arduino Mega ADK (Rev3)
  J1 = Piezo Speaker
  R1 = Resistor [tolerance=±5% resistance=220 package=THT]
  S1 = Pushbutton [package="[SMD]"]
  R2 = Resistor [tolerance=±5% resistance=10k package=THT]
  U1 = SWITCH_SPDT [package=kps-1290]
  R3 = Resistor [tolerance=±5% resistance=10k package=THT]

nets:
  N1: Part1.5V, R3.Pin_0
  N2: Part1.GND, R1.Pin_1, S1.Pin_3, S1.Pin_4, R2.Pin_1, U1.S
  N3: Part1.D2_PWM, S1.Pin_1, S1.Pin_2, R2.Pin_0
  N4: Part1.D4_PWM, U1.P, R3.Pin_1
  N5: Part1.D7_PWM, J1.pin2
  N6: J1.pin1, R1.Pin_0

notes:
  Sensor de contacto con push button y roller lever
  R1 220Ω
  R2 10kΩ
