# Fritzing sketch Schematic (Stepper Motor) (saved by Fritzing 0.9.3b)

parts:
  M1 = Stepper Motor - Unipolar
  Part1 = Arduino Mega ADK (Rev3)

nets:
  N1: M1.C, Part1.D4_PWM
  N2: M1.B, Part1.D3_PWM
  N3: M1.COMMON_2, Part1.D2_PWM
  N4: M1.D, Part1.D1/TX0

notes:
  Cable Esquema | Cable Real | Pin Arduino | Bobina
  ------------------------------------------------------------------------------------
  Negro (arriba) Negro 1 A
  Rojo Amarillo 2 B
  Amarillo Naranja 3 C
  Negro (abajo) Azul 4 D
  Unipolar PM Stepper Motor 35BY48
  Model 35BY48B06
