# Fritzing sketch Schematic (Relay and HC05) (saved by Fritzing 0.9.3b)
breadboards: 1

parts:
  KY-1 = Keyes Relay [package=THT]
  Part1 = Arduino Mega 2560 (Rev3)
  Part2 = Bluetooth HC-05 Macho  # not connected

nets:
  N1: KY-1.signal, Part1.D7_PWM

custom parts:
  Keyes Relay: The Keyes 5V relay module is suitable for SCM development, home appliance control. It uses a 5V~12V TIL control signal which can control DC / AC signal.
